# Fritzing sketch flipflop (saved by Fritzing 0.9.2b)
breadboards: 1

parts:
  R1 = Resistor [tolerance=±5% resistance=10k package="2010 [SMD]"]
  R2 = Resistor [tolerance=±5% resistance=10k package="0603 [SMD]"]
  LED1 = LED - 5mm [color="Red (633nm)" package="5 mm [THT]"]
  R3 = Resistor [tolerance=±5% resistance=4.7k package="2010 [SMD]"]
  Q2 = TRANSISTOR_NPN [part_number="P2N 2222AG" package=to-92-ammo]
  R4 = Resistor [tolerance=±5% resistance=4.7k package="2010 [SMD]"]
  R5 = Resistor [tolerance=±5% resistance=10k package="2010 [SMD]"]
  R6 = Resistor [tolerance=±5% resistance=10k package="0603 [SMD]"]
  LED2 = LED - 5mm [color="Red (633nm)" package="5 mm [THT]"]
  Q3 = TRANSISTOR_NPN [part_number="P2N 2222AG" package=to-92-ammo]

nets:
  N1: R1.Pin_0, R2.Pin_1, Q2.B
  N2: R2.Pin_0, LED1.anode, R4.Pin_1, Q3.E
  N3: LED1.cathode, Q2.C, LED2.cathode, Q3.C
  N4: R3.Pin_0, R4.Pin_0
  N5: R3.Pin_1, Q2.E, R6.Pin_0, LED2.anode
  N6: R5.Pin_0, R6.Pin_1, Q3.B
